// Logisim project brainfuck.circ as structural Verilog: 1 circuit, main circuit main
module main (
);

  wire and_1_out, and_2_out, and_3_out, and_4_out, and_5_out, button_1_out, button_2_out, button_3_out,
       button_4_out, clock_1_out, controlled_buffer_1_out, counter_1_q, decoder_1_out0, decoder_1_out1,
       decoder_1_out2, decoder_1_out3, decoder_1_out4, decoder_1_out5, decoder_1_out6, not_1_out, not_2_out,
       not_3_out, not_4_out, or_1_out, or_2_out, or_3_out, or_4_out, or_5_out;
  wire [2:0] ram_1_data;
  wire [6:0] bitselector_2_out, keyboard_1_data;
  wire [7:0] adder_1_out, bit_extender_1_out, bitselector_1_out, bitselector_3_out, ram_3_data,
       subtractor_1_out;
  wire [15:0] counter_2_q, counter_3_q, counter_4_q;

  Clock clock_1 (.out(clock_1_out));
  assign controlled_buffer_1_out = not_1_out ? clock_1_out : 1'bz;  // Controlled_Buffer controlled_buffer_1
  not not_1 (not_1_out, counter_1_q);
  and and_1 (and_1_out, clock_1_out, button_1_out, decoder_1_out5);
  Pull_Resistor pull_resistor_1 (.node(controlled_buffer_1_out));
  Counter #(.width(1), .max('h1)) counter_1 (
    .Q(counter_1_q), .clk(decoder_1_out5), .clr(or_1_out));  // open: load, D, count, carry
  or or_1 (or_1_out, and_1_out, button_2_out);
  Button button_1 (.out(button_1_out));
  Counter #(.width(16), .max('hffff)) counter_2 (
    .Q(counter_2_q), .clk(controlled_buffer_1_out), .clr(button_2_out));  // open: load, D, count, carry
  Button button_2 (.out(button_2_out));
  LED led_1 (.in(decoder_1_out5));
  Keyboard keyboard_1 (.clk(button_1_out), .clr(button_3_out), .data(keyboard_1_data));  // open: re, avail
  Button button_3 (.out(button_3_out));
  Button button_4 (.out(button_4_out));
  RAM #(.addrWidth(16), .dataWidth(3), .bus("separate")) ram_1 (
    .addr(counter_2_q), .data(ram_1_data), .clr(button_4_out));  // open: din, str, sel, clk, ld
  not not_2 (not_2_out, controlled_buffer_1_out);
  assign bit_extender_1_out = {{1{1'b0}}, keyboard_1_data};  // Bit_Extender bit_extender_1
  Decoder #(.select(3)) decoder_1 (
    .out0(decoder_1_out0), .out1(decoder_1_out1), .out2(decoder_1_out2), .out3(decoder_1_out3),
    .out4(decoder_1_out4), .out5(decoder_1_out5), .out6(decoder_1_out6), .sel(ram_1_data));  // open: out7, en
  and and_2 (and_2_out, decoder_1_out5, button_1_out);
  not not_3 (not_3_out, decoder_1_out5);
  Counter #(.width(16), .max('hffff)) counter_3 (
    .load(1'b0), .count(or_2_out), .Q(counter_3_q), .clk(and_3_out), .clr(button_2_out));  // open: D, carry
  or or_2 (or_2_out, 1'b0, decoder_1_out6);
  and and_3 (and_3_out, decoder_1_out6, not_2_out);
  and and_4 (and_4_out, clock_1_out, decoder_1_out4);
  Counter #(.width(16), .max('hffff)) counter_4 (
    .load(decoder_1_out1), .count(or_3_out), .Q(counter_4_q), .clk(not_4_out), .clr(button_2_out));  // open: D, carry
  or or_3 (or_3_out, decoder_1_out1, decoder_1_out0);
  not not_4 (not_4_out, controlled_buffer_1_out);
  BitSelector #(.width(16), .group(8)) bitselector_1 (
    .in({bitselector_3_out, bit_extender_1_out}), .out(bitselector_1_out), .sel(not_3_out));
  or or_4 (or_4_out, decoder_1_out2, decoder_1_out3);
  or or_5 (or_5_out, and_5_out, and_2_out);
  and and_5 (and_5_out, or_4_out, ~controlled_buffer_1_out);  // AND_Gate
  RAM #(.addrWidth(16), .dataWidth(16), .bus("separate")) ram_2 (
    .addr(counter_3_q), .din(counter_2_q), .str(and_3_out), .clk(and_3_out), .clr(button_2_out));  // open: data, sel, ld
  RAM #(.addrWidth(16), .bus("separate")) ram_3 (
    .addr(counter_4_q), .din(bitselector_1_out), .data(ram_3_data), .str(or_5_out), .clk(or_5_out),
    .clr(button_2_out));  // open: sel, ld
  BitSelector #(.group(7)) bitselector_2 (.in(ram_3_data), .out(bitselector_2_out), .sel(1'b0));
  Adder adder_1 (.a(ram_3_data), .b(8'h1), .out(adder_1_out));  // open: cin, cout
  Subtractor subtractor_1 (.a(ram_3_data), .b(8'h1), .out(subtractor_1_out));  // open: bin, bout
  TTY tty_1 (.data(bitselector_2_out), .clk(and_4_out), .clr(button_2_out));  // open: we
  BitSelector #(.width(16), .group(8)) bitselector_3 (
    .in({subtractor_1_out, adder_1_out}), .out(bitselector_3_out), .sel(decoder_1_out3));

  // Notes on the sheet:
  //   Записать
  //   Сброс состояния
  //   0 - >
  //   1 - <
  //   2 - +
  //   3 - -
  //   Ожидание ввода 
  //   4 - .
  //   5 - ,
  //   6 - [
  //   5 - ]
  //   Сброс программы
endmodule
